// Logisim project ula.circ as structural Verilog: 6 circuits, main circuit ula
module ula (
  input  [7:0] A,
  input  [7:0] B,
  input  OP,
  output out_4,
  output out_5,
  output out_6,
  output [7:0] R,
  output Overflow
);

  somador somador_1 (.A(A), .B(B), .R(R), .Overflow_sem_sinal(Overflow), .OP(OP));  // open: Overflow_com_sinal
  comparador comparador_1 (.A(A), .B(B), .out_3(out_4), .out_4(out_5), .out_5(out_6));

  // Notes on the sheet:
  //   para não deixar nossa ULA muito complexa, não trataremos overflow com sinal.
endmodule

module somabits (
  input  a,
  input  b,
  input  c_in,
  output s,
  output c_out
);

  wire and_1_out, and_2_out, xor_1_out;

  xor xor_1 (xor_1_out, a, b);
  xor xor_2 (s, xor_1_out, c_in);
  and and_1 (and_1_out, xor_1_out, c_in);
  and and_2 (and_2_out, a, b);
  or or_1 (c_out, and_1_out, and_2_out);

  // Notes on the sheet:
  //   a ^ b
  //   c
  //   a ^ b
  //   c
  //   a
  //   b
  //   c out = ((a^b)&c) | (a&b)
  //   s = (a^b)^c
endmodule

module somador_base (
  input  [7:0] A,
  input  c0,
  input  [7:0] B,
  output c7,
  output c8,
  output [7:0] S
);

  wire somabits_1_c_out, somabits_2_c_out, somabits_3_c_out, somabits_4_c_out, somabits_5_c_out,
       somabits_6_c_out;

  somabits somabits_1 (.a(A[0]), .b(B[0]), .c_in(c0), .s(S[0]), .c_out(somabits_1_c_out));
  somabits somabits_2 (.a(A[1]), .b(B[1]), .c_in(somabits_1_c_out), .s(S[1]), .c_out(somabits_2_c_out));
  somabits somabits_3 (.a(A[2]), .b(B[2]), .c_in(somabits_2_c_out), .s(S[2]), .c_out(somabits_3_c_out));
  somabits somabits_4 (.a(A[3]), .b(B[3]), .c_in(somabits_3_c_out), .s(S[3]), .c_out(somabits_4_c_out));
  somabits somabits_5 (.a(A[4]), .b(B[4]), .c_in(somabits_4_c_out), .s(S[4]), .c_out(somabits_5_c_out));
  somabits somabits_6 (.a(A[5]), .b(B[5]), .c_in(somabits_5_c_out), .s(S[5]), .c_out(somabits_6_c_out));
  somabits somabits_7 (.a(A[6]), .b(B[6]), .c_in(somabits_6_c_out), .s(S[6]), .c_out(c7));
  somabits somabits_8 (.a(A[7]), .b(B[7]), .c_in(c7), .s(S[7]), .c_out(c8));
endmodule

module somador (
  input  [7:0] A,
  input  [7:0] B,
  input  OP,
  output [7:0] R,
  output Overflow_com_sinal,
  output Overflow_sem_sinal
);

  wire somador_base_1_c7, somador_base_1_c8;
  wire [7:0] xor_1_out;

  xor xor_1 (xor_1_out[0], B[0], OP);
  xor xor_2 (xor_1_out[1], B[1], OP);
  xor xor_3 (xor_1_out[2], B[2], OP);
  xor xor_4 (xor_1_out[3], B[3], OP);
  xor xor_5 (xor_1_out[4], B[4], OP);
  xor xor_6 (xor_1_out[5], B[5], OP);
  xor xor_7 (xor_1_out[6], B[6], OP);
  xor xor_8 (xor_1_out[7], B[7], OP);
  somador_base somador_base_1 (.A(A), .B(xor_1_out), .c0(OP), .S(R), .c8(somador_base_1_c8), .c7(somador_base_1_c7));
  xor xor_9 (Overflow_com_sinal, somador_base_1_c7, somador_base_1_c8);
  xor xor_10 (Overflow_sem_sinal, somador_base_1_c8, OP);

  // Notes on the sheet:
  //   B_i xor OP
  //   complemento de 2 de B
  //   vai 1 caso OP seja subtração
  //   somador_base
  //   c7 ^ c8
  //   c8 ^ OP
endmodule

module comparabits (
  input  a,
  input  b,
  input  habilitador,
  output out_4,
  output out_5,
  output out_6
);

  wire and_2_out, and_3_out, not_1_out, not_2_out, not_3_out, not_4_out;

  not not_1 (not_1_out, a);
  not not_2 (not_2_out, a);
  not not_3 (not_3_out, b);
  not not_4 (not_4_out, b);
  and and_1 (out_4, not_1_out, b, habilitador);
  and and_2 (and_2_out, not_2_out, not_3_out, habilitador);
  and and_3 (and_3_out, a, b, habilitador);
  and and_4 (out_6, a, not_4_out, habilitador);
  or or_1 (out_5, and_2_out, and_3_out);

  // Notes on the sheet:
  //   (not a) & b & h
  //   a & (not b) & h
  //   ((not a) & (not b) & h) & (a & b & h)
endmodule

module comparador (
  input  [7:0] A,
  input  [7:0] B,
  output out_3,
  output out_4,
  output out_5
);

  wire comparabits_1_out_4, comparabits_1_out_5, comparabits_1_out_6, comparabits_2_out_4,
       comparabits_2_out_5, comparabits_2_out_6, comparabits_3_out_4, comparabits_3_out_5,
       comparabits_3_out_6, comparabits_4_out_4, comparabits_4_out_5, comparabits_4_out_6,
       comparabits_5_out_4, comparabits_5_out_5, comparabits_5_out_6, comparabits_6_out_4,
       comparabits_6_out_5, comparabits_6_out_6, comparabits_7_out_4, comparabits_7_out_5,
       comparabits_7_out_6, comparabits_8_out_4, comparabits_8_out_6;

  comparabits comparabits_1 (
    .a(A[7]), .b(B[7]), .habilitador(1'b1), .out_4(comparabits_1_out_4), .out_5(comparabits_1_out_5),
    .out_6(comparabits_1_out_6));
  comparabits comparabits_2 (
    .a(A[6]), .b(B[6]), .habilitador(comparabits_1_out_5), .out_4(comparabits_2_out_4),
    .out_5(comparabits_2_out_5), .out_6(comparabits_2_out_6));
  comparabits comparabits_3 (
    .a(A[5]), .b(B[5]), .habilitador(comparabits_2_out_5), .out_4(comparabits_3_out_4),
    .out_5(comparabits_3_out_5), .out_6(comparabits_3_out_6));
  comparabits comparabits_4 (
    .a(A[4]), .b(B[4]), .habilitador(comparabits_3_out_5), .out_4(comparabits_4_out_4),
    .out_5(comparabits_4_out_5), .out_6(comparabits_4_out_6));
  comparabits comparabits_5 (
    .a(A[3]), .b(B[3]), .habilitador(comparabits_4_out_5), .out_4(comparabits_5_out_4),
    .out_5(comparabits_5_out_5), .out_6(comparabits_5_out_6));
  comparabits comparabits_6 (
    .a(A[2]), .b(B[2]), .habilitador(comparabits_5_out_5), .out_4(comparabits_6_out_4),
    .out_5(comparabits_6_out_5), .out_6(comparabits_6_out_6));
  comparabits comparabits_7 (
    .a(A[1]), .b(B[1]), .habilitador(comparabits_6_out_5), .out_4(comparabits_7_out_4),
    .out_5(comparabits_7_out_5), .out_6(comparabits_7_out_6));
  comparabits comparabits_8 (
    .a(A[0]), .b(B[0]), .habilitador(comparabits_7_out_5), .out_4(comparabits_8_out_4), .out_5(out_3),
    .out_6(comparabits_8_out_6));
  or or_1 (out_4, comparabits_1_out_4, comparabits_2_out_4, comparabits_3_out_4, comparabits_4_out_4, comparabits_5_out_4, comparabits_6_out_4, comparabits_7_out_4, comparabits_8_out_4);
  or or_2 (out_5, comparabits_1_out_6, comparabits_2_out_6, comparabits_3_out_6, comparabits_4_out_6, comparabits_5_out_6, comparabits_6_out_6, comparabits_7_out_6, comparabits_8_out_6);
endmodule
